# Fritzing sketch madbox (saved by Fritzing 0.9.2b)
breadboards: 1

parts:
  R1 = Resistor [tolerance=±5% resistance=1M package="2512 [SMD]"]
  J1 = Piezo Speaker
  Part1 = Arduino Nano (Rev3.0)
  LED1 = RGB LED - (4 legs) [package="5 mm [THT]"]
  J2 = Basic Servo

nets:
  N1: R1.Pin_0, J1.pin1, Part1.GND
  N2: R1.Pin_1, J1.pin2, Part1.5V, Part1.A0
  N3: Part1.D2, LED1.blue_cathode
  N4: Part1.D3, LED1.green_cathode
  N5: Part1.D4, LED1.common_anode
  N6: Part1.D5, J2.pulse
  N7: LED1.red_cathode, J2.gnd
